// Logisim project nedonand.circ as structural Verilog: 21 circuits, main circuit main
module main (
  input  nRESET,
  output CLK1,
  output nCLK1,
  output CLK2,
  output nCLK2,
  output T1,
  output nT1,
  output T2,
  output nT2,
  output T3,
  output nT3,
  output T4,
  output nT4
);

  wire alu_1_c_prime, alu_1_d0, alu_1_d1, alu_1_d2, alu_1_d3, alu_1_nzero, alu_1_v_prime, and9_1_out_10,
       and9_2_out_10, BitALU_q, BitC_q, BitO0_q, BitO1_q, BitO2_q, clock_1_out, d_ff_3_q, d_ff_3_qn,
       d_ff_4_q, d_ff_4_qn, d_ff_5_q, d_ff_5_qn, d_ff_6_q, d_ff_6_qn, dmux8_1_o0, dmux8_1_o1, dmux8_1_o2,
       dmux8_1_o3, dmux8_1_o4, dmux8_1_o5, dmux8_1_o6, dmux8_1_o7, GO_out, halfadder_1_cout,
       halfadder_1_dout, halfadder_2_cout, halfadder_2_dout, halfadder_3_cout, halfadder_3_dout,
       halfadder_4_cout, halfadder_4_dout, halfadder_5_cout, halfadder_5_dout, halfadder_6_cout,
       halfadder_6_dout, halfadder_7_cout, halfadder_7_dout, halfadder_8_cout, halfadder_8_dout,
       halfadder_9_cout, halfadder_9_dout, halfadder_10_cout, halfadder_10_dout, halfadder_11_dout,
       halfadder_12_cout, halfadder_12_dout, nand_1_out, nand_2_out, nand_3_out, nand_4_out, nand_5_out,
       nand_6_out, nand_7_out, nand_8_out, nand_9_out, nand_10_out, nand_11_out, nand_12_out, nand_13_out,
       nand_14_out, nand_15_out, nand_16_out, nand_17_out, nand_18_out, nand_19_out, nand_20_out,
       nand_21_out, nand_22_out, nand_23_out, nand_24_out, nand_25_out, nand_26_out, nand_27_out,
       nand_28_out, nand_29_out, nand_30_out, nand_31_out, nand_32_out, nand_33_out, nand_34_out,
       nand_35_out, nand_36_out, nand_37_out, nand_38_out, nand_39_out, nand_48_out, nand_49_out,
       nand_50_out, nand_51_out, nand_52_out, nand_53_out, nand_54_out, nand_55_out, nand_56_out,
       nand_57_out, nand_58_out, nand_59_out, nand_60_out, nand_61_out, nand_62_out, nand_63_out,
       nand_64_out, nand_65_out, nand_66_out, nand_67_out, nand_68_out, nand_69_out, nand_70_out,
       nand_71_out, nand_72_out, nand_73_out, nand_74_out, nand_83_out, nand_84_out, nand_85_out,
       nand_86_out, nand_87_out, nand_88_out, nand_89_out, nand_90_out, nand_91_out, nand_92_out,
       nand_93_out, nand_94_out, nand_95_out, nand_96_out, nand_97_out, nand_98_out, nand_99_out,
       nand_100_out, nand_101_out, nand_102_out, nand_103_out, nand_104_out, nand_105_out, nand_106_out,
       nand_107_out, nand_108_out, nand_109_out, nand_110_out, nand_111_out, nand_112_out, nand_113_out,
       nand_114_out, nand_115_out, nand_116_out, nand_117_out, nand_118_out, nand_119_out, nand_120_out,
       nand_121_out, nand_122_out, nand_123_out, nand_124_out, nand_125_out, nand_126_out, nand_127_out,
       nand_128_out, nand_129_out, nand_130_out, nand_131_out, nand_132_out, nand_133_out, nand_134_out,
       nand_135_out, nand_136_out, nand_137_out, nand_138_out, nand_139_out, nand_140_out, nand_141_out,
       nand_142_out, nand_143_out, nand_144_out, nand_145_out, nand_146_out, nand_147_out, nand_148_out,
       nand_149_out, nand_150_out, nand_151_out, nand_152_out, nand_153_out, nand_154_out, nand_155_out,
       nand_156_out, nand_157_out, nand_158_out, nand_159_out, nand_160_out, nand_161_out, nand_162_out,
       nand_163_out, nand_164_out, nand_165_out, nand_166_out, nand_167_out, nand_168_out, nand_169_out,
       nand_170_out, nand_171_out, nand_172_out, nand_173_out, nand_174_out, nand_175_out, nand_176_out,
       nand_177_out, nand_178_out, nand_179_out, nand_180_out, nand_181_out, nand_182_out, nand_183_out,
       nand_184_out, nand_185_out, nand_186_out, nand_187_out, nand_188_out, nand_189_out, nand_190_out,
       nand_191_out, nand_192_out, nand_193_out, nand_194_out, nand_195_out, nand_196_out, nand_197_out,
       nand_198_out, nand_199_out, nand_200_out, nand_201_out, nand_202_out, nand_203_out, nand_212_out,
       nand_213_out, nand_214_out, nand_215_out, nand_216_out, nand_217_out, nand_218_out, nand_219_out,
       not_1_out, not_2_out, not_3_out, not_4_out, not_5_out, not_6_out, not_7_out, s_r_ff_1_q, s_r_ff_2_q,
       xor_1_out, xor_2_out, xor_3_out, xor_4_out, xor_5_out;
  wire [2:0] rom_1_data_2;
  wire [3:0] rom_1_data;
  wire [7:0] multiplexer_1_out, multiplexer_2_out, multiplexer_3_out, multiplexer_4_out, multiplexer_5_out,
       multiplexer_6_out, multiplexer_7_out, nand_75_out, nand_204_out, not_8_out, not_9_out,
       Reg_A_prime_prime_q, Reg_A_prime_q, Reg_A_q, Reg_B_q, Reg_C_q, Reg_D_q, Reg_E_q, Reg_F_P8_q,
       Reg_R_prime_prime_q, Reg_R_prime_q, Reg_T_q;
  wire [7:7] rom_1_data_3;
  wire [10:0] PC8_q;

  Clock clock_1 (.out(clock_1_out));
  Button GO (.out(GO_out));
  not not_1 (not_1_out, nand_5_out);
  not not_2 (not_2_out, nand_6_out);
  not not_3 (not_3_out, GO_out);
  S_R_Flip_Flop s_r_ff_1 (
    .S(not_1_out), .clk(not_4_out), .R(not_2_out), .Q(s_r_ff_1_q));  // open: Qn, preset, reset, en
  nand nand_1 (nand_1_out, halfadder_12_cout, s_r_ff_1_q);
  nand nand_2 (nand_2_out, not_3_out, nRESET);
  not not_4 (not_4_out, clock_1_out);
  not not_5 (not_5_out, nRESET);
  nand nand_3 (nand_3_out, s_r_ff_2_q, s_r_ff_2_q);
  nand nand_4 (nand_4_out, nand_1_out, nand_1_out);
  nand nand_5 (nand_5_out, nand_2_out, nand_2_out);
  halfadder halfadder_1 (.A(nand_4_out), .B(PC8_q[0]), .DOUT(halfadder_1_dout), .COUT(halfadder_1_cout));
  halfadder halfadder_2 (.A(halfadder_1_cout), .B(PC8_q[1]), .DOUT(halfadder_2_dout), .COUT(halfadder_2_cout));
  halfadder halfadder_3 (.A(halfadder_2_cout), .B(PC8_q[2]), .DOUT(halfadder_3_dout), .COUT(halfadder_3_cout));
  halfadder halfadder_4 (.A(halfadder_3_cout), .B(PC8_q[3]), .DOUT(halfadder_4_dout), .COUT(halfadder_4_cout));
  halfadder halfadder_5 (.A(halfadder_4_cout), .B(PC8_q[4]), .DOUT(halfadder_5_dout), .COUT(halfadder_5_cout));
  halfadder halfadder_6 (.A(halfadder_5_cout), .B(PC8_q[5]), .DOUT(halfadder_6_dout), .COUT(halfadder_6_cout));
  halfadder halfadder_7 (.A(halfadder_6_cout), .B(PC8_q[6]), .DOUT(halfadder_7_dout), .COUT(halfadder_7_cout));
  halfadder halfadder_8 (.A(halfadder_7_cout), .B(PC8_q[7]), .DOUT(halfadder_8_dout), .COUT(halfadder_8_cout));
  halfadder halfadder_9 (.A(halfadder_8_cout), .B(PC8_q[8]), .DOUT(halfadder_9_dout), .COUT(halfadder_9_cout));
  halfadder halfadder_10 (.A(halfadder_9_cout), .B(PC8_q[9]), .DOUT(halfadder_10_dout), .COUT(halfadder_10_cout));
  halfadder halfadder_11 (.A(halfadder_10_cout), .B(PC8_q[10]), .DOUT(halfadder_11_dout));  // open: COUT
  nand nand_6 (nand_6_out, dmux8_1_o0, s_r_ff_1_q);
  nand nand_7 (nand_7_out, nand_3_out, multiplexer_7_out[0]);
  nand nand_8 (nand_8_out, s_r_ff_2_q, halfadder_1_dout);
  nand nand_9 (nand_9_out, nand_3_out, multiplexer_7_out[1]);
  nand nand_10 (nand_10_out, s_r_ff_2_q, halfadder_2_dout);
  nand nand_11 (nand_11_out, nand_3_out, multiplexer_7_out[2]);
  nand nand_12 (nand_12_out, s_r_ff_2_q, halfadder_3_dout);
  nand nand_13 (nand_13_out, nand_3_out, multiplexer_7_out[3]);
  nand nand_14 (nand_14_out, s_r_ff_2_q, halfadder_4_dout);
  nand nand_15 (nand_15_out, nand_3_out, multiplexer_7_out[4]);
  nand nand_16 (nand_16_out, s_r_ff_2_q, halfadder_5_dout);
  nand nand_17 (nand_17_out, nand_3_out, multiplexer_7_out[5]);
  nand nand_18 (nand_18_out, s_r_ff_2_q, halfadder_6_dout);
  nand nand_19 (nand_19_out, nand_3_out, multiplexer_7_out[6]);
  nand nand_20 (nand_20_out, s_r_ff_2_q, halfadder_7_dout);
  nand nand_21 (nand_21_out, nand_3_out, multiplexer_7_out[7]);
  nand nand_22 (nand_22_out, s_r_ff_2_q, halfadder_8_dout);
  nand nand_23 (nand_23_out, nand_3_out, Reg_F_P8_q[0]);
  nand nand_24 (nand_24_out, s_r_ff_2_q, halfadder_9_dout);
  nand nand_25 (nand_25_out, nand_3_out, Reg_F_P8_q[1]);
  nand nand_26 (nand_26_out, s_r_ff_2_q, halfadder_10_dout);
  nand nand_27 (nand_27_out, nand_3_out, Reg_F_P8_q[2]);
  nand nand_28 (nand_28_out, s_r_ff_2_q, halfadder_11_dout);
  halfadder halfadder_12 (.A(CLK1), .B(CLK2), .DOUT(halfadder_12_dout), .COUT(halfadder_12_cout));
  nand nand_29 (nand_29_out, nand_7_out, nand_8_out);
  nand nand_30 (nand_30_out, nand_9_out, nand_10_out);
  nand nand_31 (nand_31_out, nand_11_out, nand_12_out);
  nand nand_32 (nand_32_out, nand_13_out, nand_14_out);
  nand nand_33 (nand_33_out, nand_15_out, nand_16_out);
  nand nand_34 (nand_34_out, nand_17_out, nand_18_out);
  nand nand_35 (nand_35_out, nand_19_out, nand_20_out);
  nand nand_36 (nand_36_out, nand_21_out, nand_22_out);
  nand nand_37 (nand_37_out, nand_23_out, nand_24_out);
  nand nand_38 (nand_38_out, nand_25_out, nand_26_out);
  nand nand_39 (nand_39_out, nand_27_out, nand_28_out);
  D_Flip_Flop d_ff_1 (.clk(clock_1_out), .D(nCLK1), .Q(CLK1), .Qn(nCLK1), .reset(not_5_out));  // open: preset, en
  D_Flip_Flop d_ff_2 (
    .clk(clock_1_out), .D(halfadder_12_dout), .Q(CLK2), .Qn(nCLK2), .reset(not_5_out));  // open: preset, en
  D_Flip_Flop PC0 (.clk(nT4), .D(nand_29_out), .Q(PC8_q[0]), .reset(not_5_out));  // open: Qn, preset, en
  D_Flip_Flop PC1 (.clk(nT4), .D(nand_30_out), .Q(PC8_q[1]), .reset(not_5_out));  // open: Qn, preset, en
  D_Flip_Flop PC2 (.clk(nT4), .D(nand_31_out), .Q(PC8_q[2]), .reset(not_5_out));  // open: Qn, preset, en
  D_Flip_Flop PC3 (.clk(nT4), .D(nand_32_out), .Q(PC8_q[3]), .reset(not_5_out));  // open: Qn, preset, en
  D_Flip_Flop PC4 (.clk(nT4), .D(nand_33_out), .Q(PC8_q[4]), .reset(not_5_out));  // open: Qn, preset, en
  D_Flip_Flop PC5 (.clk(nT4), .D(nand_34_out), .Q(PC8_q[5]), .reset(not_5_out));  // open: Qn, preset, en
  D_Flip_Flop PC6 (.clk(nT4), .D(nand_35_out), .Q(PC8_q[6]), .reset(not_5_out));  // open: Qn, preset, en
  D_Flip_Flop PC7 (.clk(nT4), .D(nand_36_out), .Q(PC8_q[7]), .reset(not_5_out));  // open: Qn, preset, en
  D_Flip_Flop PC8 (.clk(nT4), .D(nand_37_out), .Q(PC8_q[8]), .reset(not_5_out));  // open: Qn, preset, en
  D_Flip_Flop PC9 (.clk(nT4), .D(nand_38_out), .Q(PC8_q[9]), .reset(not_5_out));  // open: Qn, preset, en
  D_Flip_Flop PC10 (.clk(nT4), .D(nand_39_out), .Q(PC8_q[10]), .reset(not_5_out));  // open: Qn, preset, en
  not not_6 (not_6_out, nT2);
  not not_7 (not_7_out, nand_128_out);
  S_R_Flip_Flop s_r_ff_2 (
    .S(not_6_out), .clk(not_4_out), .R(not_7_out), .Q(s_r_ff_2_q));  // open: Qn, preset, reset, en
  nand nand_40 (nT1, nCLK1, nCLK2);
  nand nand_41 (nT2, nCLK2, CLK1);
  nand nand_42 (nT3, nCLK1, CLK2);
  nand nand_43 (nT4, CLK2, CLK1);
  nand nand_44 (T1, nT1, nT1);
  nand nand_45 (T2, nT2, nT2);
  nand nand_46 (T3, nT3, nT3);
  nand nand_47 (T4, nT4, nT4);
  Hex_Digit_Display hex_digit_display_1 (.value(PC8_q[7:4]));  // open: dp
  Hex_Digit_Display hex_digit_display_2 (.value({1'b0, PC8_q[10:8]}));  // open: dp
  Hex_Digit_Display hex_digit_display_3 (.value(rom_1_data));  // open: dp
  LED led_1 (.in(T2));
  LED led_2 (.in(T1));
  ROM #(.addrWidth(11)) rom_1 (.addr(PC8_q), .data({rom_1_data, rom_1_data_3[7], rom_1_data_2}));  // open: sel
  Hex_Digit_Display hex_digit_display_4 (.value(PC8_q[3:0]));  // open: dp
  Hex_Digit_Display hex_digit_display_5 (.value({rom_1_data_3[7], rom_1_data_2}));  // open: dp
  LED led_3 (.in(T3));
  LED led_4 (.in(T4));
  nand nand_48 (nand_48_out, rom_1_data_3[7], rom_1_data[1]);
  nand nand_49 (nand_49_out, rom_1_data[0], rom_1_data[0]);
  nand nand_50 (nand_50_out, rom_1_data_2[0], rom_1_data_2[0]);
  nand nand_51 (nand_51_out, rom_1_data_2[1], rom_1_data_2[1]);
  nand nand_52 (nand_52_out, rom_1_data_2[2], rom_1_data_2[2]);
  nand nand_53 (nand_53_out, rom_1_data[0], rom_1_data[0]);
  nand nand_54 (nand_54_out, rom_1_data[1], rom_1_data[1]);
  nand nand_55 (nand_55_out, rom_1_data[2], rom_1_data[2]);
  nand nand_56 (nand_56_out, nand_48_out, nand_48_out);
  nand nand_57 (nand_57_out, rom_1_data[2], rom_1_data[3]);
  nand nand_58 (nand_58_out, rom_1_data[3], rom_1_data[3]);
  nand nand_59 (nand_59_out, nand_58_out, rom_1_data_2[0]);
  nand nand_60 (nand_60_out, rom_1_data[3], multiplexer_7_out[0]);
  nand nand_61 (nand_61_out, nand_58_out, rom_1_data_2[1]);
  nand nand_62 (nand_62_out, rom_1_data[3], multiplexer_7_out[1]);
  nand nand_63 (nand_63_out, nand_58_out, rom_1_data_2[2]);
  nand nand_64 (nand_64_out, rom_1_data[3], multiplexer_7_out[2]);
  nand nand_65 (nand_65_out, nand_58_out, rom_1_data_3[7]);
  nand nand_66 (nand_66_out, rom_1_data[3], multiplexer_7_out[3]);
  nand nand_67 (nand_67_out, nand_58_out, rom_1_data[0]);
  nand nand_68 (nand_68_out, rom_1_data[3], multiplexer_7_out[4]);
  nand nand_69 (nand_69_out, nand_58_out, rom_1_data[1]);
  nand nand_70 (nand_70_out, rom_1_data[3], multiplexer_7_out[5]);
  nand nand_71 (nand_71_out, nand_58_out, rom_1_data[2]);
  nand nand_72 (nand_72_out, rom_1_data[3], multiplexer_7_out[6]);
  nand nand_73 (nand_73_out, nand_58_out, rom_1_data[3]);
  nand nand_74 (nand_74_out, rom_1_data[3], multiplexer_7_out[7]);
  and9 and9_1 (
    .in_1(nand_50_out), .in_2(nand_51_out), .in_3(nand_52_out), .in_4(rom_1_data_3[7]), .in_5(nand_53_out),
    .in_6(nand_54_out), .in_7(nand_55_out), .in_8(rom_1_data[3]), .in_9(rom_1_data[3]), .out_10(and9_1_out_10));
  \xor  xor_1 (.A(rom_1_data_2[0]), .B(rom_1_data_3[7]), .OUT(xor_1_out));
  \xor  xor_2 (.A(rom_1_data_2[1]), .B(rom_1_data[0]), .OUT(xor_2_out));
  \xor  xor_3 (.A(rom_1_data_2[2]), .B(rom_1_data[1]), .OUT(xor_3_out));
  nand nand_75 (nand_75_out[0], nand_59_out, nand_60_out);
  nand nand_76 (nand_75_out[1], nand_61_out, nand_62_out);
  nand nand_77 (nand_75_out[2], nand_63_out, nand_64_out);
  nand nand_78 (nand_75_out[3], nand_65_out, nand_66_out);
  nand nand_79 (nand_75_out[4], nand_67_out, nand_68_out);
  nand nand_80 (nand_75_out[5], nand_69_out, nand_70_out);
  nand nand_81 (nand_75_out[6], nand_71_out, nand_72_out);
  nand nand_82 (nand_75_out[7], nand_73_out, nand_74_out);
  nand nand_83 (nand_83_out, and9_1_out_10, and9_1_out_10);
  nand nand_84 (nand_84_out, xor_1_out, xor_1_out);
  nand nand_85 (nand_85_out, xor_2_out, xor_2_out);
  nand nand_86 (nand_86_out, xor_3_out, xor_3_out);
  nand nand_87 (nand_87_out, nand_57_out, nand_57_out);
  nand nand_88 (nand_88_out, rom_1_data[2], rom_1_data[2]);
  nand nand_89 (nand_89_out, rom_1_data[3], nand_88_out);
  nand nand_90 (nand_90_out, nand_87_out, nand_49_out);
  nand nand_91 (nand_91_out, rom_1_data_3[7], rom_1_data[3]);
  nand nand_92 (nand_92_out, rom_1_data[0], rom_1_data[3]);
  nand nand_93 (nand_93_out, rom_1_data[1], rom_1_data[3]);
  nand nand_94 (nand_94_out, T4, nand_57_out);
  nand nand_95 (nand_95_out, nand_84_out, nand_85_out);
  nand nand_96 (nand_96_out, nand_89_out, nand_89_out);
  nand nand_97 (nand_97_out, nand_90_out, nand_90_out);
  nand nand_98 (nand_98_out, nand_97_out, nand_56_out);
  nand nand_99 (nand_99_out, dmux8_1_o1, nand_83_out);
  nand nand_100 (nand_100_out, nand_218_out, nand_218_out);
  nand nand_101 (nand_101_out, nand_109_out, nand_75_out[7]);
  nand nand_102 (nand_102_out, nand_218_out, nand_204_out[7]);
  nand nand_103 (nand_103_out, nand_109_out, nand_75_out[6]);
  nand nand_104 (nand_104_out, nand_218_out, and9_2_out_10);
  nand nand_105 (nand_105_out, nand_109_out, nand_75_out[5]);
  nand nand_106 (nand_106_out, nand_218_out, alu_1_v_prime);
  nand nand_107 (nand_107_out, nand_109_out, nand_75_out[4]);
  nand nand_108 (nand_108_out, nand_218_out, alu_1_c_prime);
  nand nand_109 (nand_109_out, nand_218_out, nand_218_out);
  nand nand_110 (nand_110_out, nand_219_out, nand_219_out);
  nand nand_111 (nand_111_out, rom_1_data[3], nand_91_out);
  nand nand_112 (nand_112_out, nand_92_out, nand_92_out);
  nand nand_113 (nand_113_out, nand_93_out, nand_93_out);
  nand nand_114 (nand_114_out, nand_94_out, nand_94_out);
  nand nand_115 (nand_115_out, nand_95_out, nand_95_out);
  nand nand_116 (nand_116_out, nand_99_out, nand_100_out);
  nand nand_117 (nand_117_out, nand_57_out, BitALU_q);
  nand nand_118 (nand_118_out, nand_101_out, nand_102_out);
  nand nand_119 (nand_119_out, nand_103_out, nand_104_out);
  nand nand_120 (nand_120_out, nand_105_out, nand_106_out);
  nand nand_121 (nand_121_out, nand_107_out, nand_108_out);
  nand nand_122 (nand_122_out, dmux8_1_o6, dmux8_1_o6);
  nand nand_123 (nand_123_out, nand_218_out, nand_218_out);
  nand nand_124 (nand_124_out, nand_110_out, nand_75_out[3]);
  nand nand_125 (nand_125_out, nand_219_out, alu_1_c_prime);
  nand nand_126 (nand_126_out, dmux8_1_o6, dmux8_1_o6);
  nand nand_127 (nand_127_out, nand_219_out, nand_219_out);
  dmux8 dmux8_1 (
    .A0(nand_111_out), .A1(nand_112_out), .A2(nand_113_out), .IN(nand_114_out), .O0(dmux8_1_o0),
    .O1(dmux8_1_o1), .O2(dmux8_1_o2), .O3(dmux8_1_o3), .O4(dmux8_1_o4), .O5(dmux8_1_o5), .O6(dmux8_1_o6),
    .O7(dmux8_1_o7));
  nand nand_128 (nand_128_out, dmux8_1_o7, dmux8_1_o7);
  nand nand_129 (nand_129_out, nand_115_out, nand_86_out);
  nand nand_130 (nand_130_out, nand_129_out, nand_129_out);
  nand nand_131 (nand_131_out, nand_130_out, nand_96_out);
  nand nand_132 (nand_132_out, nand_131_out, nand_98_out);
  Multiplexer #(.width(8)) multiplexer_1 (
    .in0(multiplexer_6_out), .in1(nand_75_out), .out(multiplexer_1_out), .sel(nand_117_out));  // open: en
  nand nand_133 (nand_133_out, nand_118_out, nand_118_out);
  nand nand_134 (nand_134_out, nand_133_out, nand_133_out);
  nand nand_135 (nand_135_out, nand_119_out, nand_119_out);
  nand nand_136 (nand_136_out, nand_135_out, nand_135_out);
  nand nand_137 (nand_137_out, nand_120_out, nand_120_out);
  nand nand_138 (nand_138_out, nand_137_out, nand_137_out);
  nand nand_139 (nand_139_out, nand_121_out, nand_121_out);
  nand nand_140 (nand_140_out, nand_139_out, nand_139_out);
  nand nand_141 (nand_141_out, nand_122_out, nand_123_out);
  nand nand_142 (nand_142_out, nand_124_out, nand_125_out);
  nand nand_143 (nand_143_out, nand_126_out, nand_127_out);
  Register #(.trigger("high")) Reg_A (.D(multiplexer_1_out), .Q(Reg_A_q), .clk(nand_116_out));  // open: en, clr
  Register #(.trigger("high")) Reg_B (.D(nand_75_out), .Q(Reg_B_q), .clk(dmux8_1_o2));  // open: en, clr
  Register #(.trigger("high")) Reg_C (.D(nand_75_out), .Q(Reg_C_q), .clk(dmux8_1_o3));  // open: en, clr
  Register #(.trigger("high")) Reg_D (.D(nand_75_out), .Q(Reg_D_q), .clk(dmux8_1_o4));  // open: en, clr
  Register #(.trigger("high")) Reg_E (.D(nand_75_out), .Q(Reg_E_q), .clk(dmux8_1_o5));  // open: en, clr
  D_Flip_Flop #(.trigger("high")) Reg_F_S (
    .clk(nand_141_out), .D(nand_134_out), .Q(Reg_F_P8_q[7]));  // open: Qn, preset, en, reset
  D_Flip_Flop #(.trigger("high")) Reg_F_Z (
    .clk(nand_141_out), .D(nand_136_out), .Q(Reg_F_P8_q[6]));  // open: Qn, preset, en, reset
  D_Flip_Flop #(.trigger("high")) Reg_F_V (
    .clk(nand_141_out), .D(nand_138_out), .Q(Reg_F_P8_q[5]));  // open: Qn, preset, en, reset
  D_Flip_Flop #(.trigger("high")) Reg_F_C (
    .clk(nand_141_out), .D(nand_140_out), .Q(Reg_F_P8_q[4]));  // open: Qn, preset, en, reset
  D_Flip_Flop #(.trigger("high")) Reg_F_H (
    .clk(nand_143_out), .D(nand_144_out), .Q(Reg_F_P8_q[3]));  // open: Qn, preset, en, reset
  nand nand_144 (nand_144_out, nand_145_out, nand_145_out);
  nand nand_145 (nand_145_out, nand_142_out, nand_142_out);
  D_Flip_Flop #(.trigger("high")) Reg_F_P10 (
    .clk(dmux8_1_o6), .D(nand_75_out[2]), .Q(Reg_F_P8_q[2]));  // open: Qn, preset, en, reset
  D_Flip_Flop #(.trigger("high")) Reg_F_P9 (
    .clk(dmux8_1_o6), .D(nand_75_out[1]), .Q(Reg_F_P8_q[1]));  // open: Qn, preset, en, reset
  D_Flip_Flop #(.trigger("high")) Reg_F_P8 (
    .clk(dmux8_1_o6), .D(nand_75_out[0]), .Q(Reg_F_P8_q[0]));  // open: Qn, preset, en, reset
  _7_Segment_Display u_7_segment_display_1 (
    .g(Reg_A_q[6]), .f(Reg_A_q[5]), .a(Reg_A_q[0]), .b(Reg_A_q[1]), .e(Reg_A_q[4]), .d(Reg_A_q[3]),
    .c(Reg_A_q[2]), .dp(Reg_A_q[7]));
  _7_Segment_Display u_7_segment_display_2 (
    .g(Reg_B_q[6]), .f(Reg_B_q[5]), .a(Reg_B_q[0]), .b(Reg_B_q[1]), .e(Reg_B_q[4]), .d(Reg_B_q[3]),
    .c(Reg_B_q[2]), .dp(Reg_B_q[7]));
  Multiplexer #(.select(3), .width(8)) multiplexer_2 (
    .in0({8{1'b0}}), .in1(Reg_A_q), .in2(Reg_B_q), .in3(Reg_C_q), .in4(Reg_D_q), .in5(Reg_E_q),
    .in6(Reg_F_P8_q), .in7(PC8_q[7:0]), .out(multiplexer_2_out), .sel(rom_1_data_2));  // open: en
  _7_Segment_Display u_7_segment_display_3 (
    .g(Reg_C_q[6]), .f(Reg_C_q[5]), .a(Reg_C_q[0]), .b(Reg_C_q[1]), .e(Reg_C_q[4]), .d(Reg_C_q[3]),
    .c(Reg_C_q[2]), .dp(Reg_C_q[7]));
  Register #(.trigger("high")) Reg_T (.D(multiplexer_2_out), .Q(Reg_T_q), .clk(T3));  // open: en, clr
  nand nand_146 (nand_146_out, rom_1_data_2[2], rom_1_data_2[2]);
  nand nand_147 (nand_147_out, rom_1_data_2[1], rom_1_data_2[1]);
  nand nand_148 (nand_148_out, nand_152_out, nand_152_out);
  nand nand_149 (nand_149_out, nand_148_out, rom_1_data_2[0]);
  nand nand_150 (nand_150_out, nand_149_out, nand_159_out);
  nand nand_151 (nand_151_out, nand_131_out, nand_131_out);
  _7_Segment_Display u_7_segment_display_4 (
    .g(Reg_D_q[6]), .f(Reg_D_q[5]), .a(Reg_D_q[0]), .b(Reg_D_q[1]), .e(Reg_D_q[4]), .d(Reg_D_q[3]),
    .c(Reg_D_q[2]), .dp(Reg_D_q[7]));
  Multiplexer #(.width(8)) multiplexer_3 (
    .in0(Reg_T_q), .in1(not_8_out), .out(multiplexer_3_out), .sel(nand_132_out));  // open: en
  assign not_8_out = ~Reg_T_q;  // NOT_Gate not_8, 8 bits wide
  nand nand_152 (nand_152_out, nand_146_out, nand_147_out);
  Multiplexer #(.width(8)) multiplexer_4 (
    .in0(nand_204_out), .in1(Reg_A_q), .out(multiplexer_4_out), .sel(nand_159_out));  // open: en
  nand nand_153 (nand_153_out, nand_149_out, nand_149_out);
  assign not_9_out = ~nand_204_out;  // NOT_Gate not_9, 8 bits wide
  nand nand_154 (nand_154_out, nand_150_out, BitALU_q);
  nand nand_155 (nand_155_out, nand_153_out, nand_151_out);
  _7_Segment_Display u_7_segment_display_5 (
    .g(Reg_E_q[6]), .f(Reg_E_q[5]), .a(Reg_E_q[0]), .b(Reg_E_q[1]), .e(Reg_E_q[4]), .d(Reg_E_q[3]),
    .c(Reg_E_q[2]), .dp(Reg_E_q[7]));
  Multiplexer #(.width(8)) multiplexer_5 (
    .in0({{5{rom_1_data_3[7]}}, rom_1_data_2}), .in1(multiplexer_3_out), .out(multiplexer_5_out),
    .sel(nand_156_out));  // open: en
  Multiplexer #(.width(8)) multiplexer_6 (
    .in0(not_9_out), .in1(nand_204_out), .out(multiplexer_6_out), .sel(nand_155_out));  // open: en
  Multiplexer #(.width(8)) multiplexer_7 (
    .in0(multiplexer_6_out), .in1(multiplexer_3_out), .out(multiplexer_7_out), .sel(nand_154_out));  // open: en
  nand nand_156 (nand_156_out, rom_1_data[1], rom_1_data[0]);
  nand nand_157 (nand_157_out, nand_87_out, T4);
  nand nand_158 (nand_158_out, nand_157_out, nand_157_out);
  Register #(.trigger("high")) Reg_R_prime_prime (
    .D(Reg_R_prime_q), .Q(Reg_R_prime_prime_q), .clk(T1));  // open: en, clr
  Register #(.trigger("high")) Reg_R_prime (
    .D(multiplexer_5_out), .Q(Reg_R_prime_q), .clk(nand_158_out));  // open: en, clr
  Register #(.trigger("high")) Reg_A_prime (
    .D(multiplexer_4_out), .Q(Reg_A_prime_q), .clk(nand_158_out));  // open: en, clr
  LED led_5 (.in(T1));
  LED led_6 (.in(T2));
  LED led_7 (.in(T3));
  LED led_8 (.in(nCLK2));
  LED led_9 (.in(CLK2));
  \xor  xor_4 (.A(nCLK2), .B(alu_1_nzero), .OUT(xor_4_out));
  \xor  xor_5 (.A(CLK2), .B(alu_1_nzero), .OUT(xor_5_out));
  D_Flip_Flop BitO0 (.clk(T1), .D(rom_1_data_3[7]), .Q(BitO0_q));  // open: Qn, preset, en, reset
  D_Flip_Flop BitO1 (.clk(T1), .D(rom_1_data[0]), .Q(BitO1_q));  // open: Qn, preset, en, reset
  D_Flip_Flop BitO2 (.clk(T1), .D(rom_1_data[1]), .Q(BitO2_q));  // open: Qn, preset, en, reset
  nand nand_159 (nand_159_out, nand_87_out, BitALU_q);
  D_Flip_Flop BitALU (.clk(T1), .D(nand_87_out), .Q(BitALU_q));  // open: Qn, preset, en, reset
  D_Flip_Flop BitC (.clk(T1), .D(Reg_F_P8_q[4]), .Q(BitC_q));  // open: Qn, preset, en, reset
  Register #(.trigger("high")) Reg_A_prime_prime (
    .D(Reg_A_prime_q), .Q(Reg_A_prime_prime_q), .clk(T1));  // open: en, clr
  LED led_10 (.in(T4));
  nand nand_160 (nand_160_out, nCLK2, BitC_q);
  nand nand_161 (nand_161_out, CLK2, Reg_F_P8_q[3]);
  nand nand_162 (nand_162_out, xor_5_out, Reg_R_prime_prime_q[0]);
  nand nand_163 (nand_163_out, xor_4_out, Reg_R_prime_prime_q[4]);
  nand nand_164 (nand_164_out, xor_5_out, Reg_R_prime_prime_q[1]);
  nand nand_165 (nand_165_out, xor_4_out, Reg_R_prime_prime_q[5]);
  nand nand_166 (nand_166_out, xor_5_out, Reg_R_prime_prime_q[2]);
  nand nand_167 (nand_167_out, xor_4_out, Reg_R_prime_prime_q[6]);
  nand nand_168 (nand_168_out, xor_5_out, Reg_R_prime_prime_q[3]);
  nand nand_169 (nand_169_out, xor_4_out, Reg_R_prime_prime_q[7]);
  nand nand_170 (nand_170_out, xor_5_out, Reg_A_prime_prime_q[0]);
  nand nand_171 (nand_171_out, xor_4_out, Reg_A_prime_prime_q[4]);
  nand nand_172 (nand_172_out, xor_5_out, Reg_A_prime_prime_q[1]);
  nand nand_173 (nand_173_out, xor_4_out, Reg_A_prime_prime_q[5]);
  nand nand_174 (nand_174_out, xor_5_out, Reg_A_prime_prime_q[2]);
  nand nand_175 (nand_175_out, xor_4_out, Reg_A_prime_prime_q[6]);
  nand nand_176 (nand_176_out, xor_5_out, Reg_A_prime_prime_q[3]);
  nand nand_177 (nand_177_out, xor_4_out, Reg_A_prime_prime_q[7]);
  nand nand_178 (nand_178_out, nand_160_out, nand_161_out);
  nand nand_179 (nand_179_out, nand_162_out, nand_163_out);
  nand nand_180 (nand_180_out, nand_164_out, nand_165_out);
  nand nand_181 (nand_181_out, nand_166_out, nand_167_out);
  nand nand_182 (nand_182_out, nand_168_out, nand_169_out);
  nand nand_183 (nand_183_out, nand_170_out, nand_171_out);
  nand nand_184 (nand_184_out, nand_172_out, nand_173_out);
  nand nand_185 (nand_185_out, nand_174_out, nand_175_out);
  nand nand_186 (nand_186_out, nand_176_out, nand_177_out);
  alu alu_1 (
    .O0(BitO0_q), .O1(BitO1_q), .O2(BitO2_q), .A0(nand_183_out), .A1(nand_184_out), .A2(nand_185_out),
    .A3(nand_186_out), .B0(nand_179_out), .B1(nand_180_out), .B2(nand_181_out), .B3(nand_182_out),
    .C(nand_178_out), .V_prime(alu_1_v_prime), .C_prime(alu_1_c_prime), .D0(alu_1_d0), .D1(alu_1_d1),
    .D2(alu_1_d2), .D3(alu_1_d3), .nZERO(alu_1_nzero));
  nand nand_187 (nand_187_out, alu_1_nzero, alu_1_nzero);
  D_Flip_Flop #(.trigger("high")) d_ff_3 (
    .clk(T2), .D(alu_1_d0), .Q(d_ff_3_q), .Qn(d_ff_3_qn));  // open: preset, en, reset
  D_Flip_Flop #(.trigger("high")) d_ff_4 (
    .clk(T2), .D(alu_1_d1), .Q(d_ff_4_q), .Qn(d_ff_4_qn));  // open: preset, en, reset
  D_Flip_Flop #(.trigger("high")) d_ff_5 (
    .clk(T2), .D(alu_1_d2), .Q(d_ff_5_q), .Qn(d_ff_5_qn));  // open: preset, en, reset
  D_Flip_Flop #(.trigger("high")) d_ff_6 (
    .clk(T2), .D(alu_1_d3), .Q(d_ff_6_q), .Qn(d_ff_6_qn));  // open: preset, en, reset
  nand nand_188 (nand_188_out, alu_1_nzero, d_ff_3_q);
  nand nand_189 (nand_189_out, nand_187_out, alu_1_d0);
  nand nand_190 (nand_190_out, alu_1_nzero, d_ff_4_q);
  nand nand_191 (nand_191_out, nand_187_out, alu_1_d1);
  nand nand_192 (nand_192_out, alu_1_nzero, d_ff_5_q);
  nand nand_193 (nand_193_out, nand_187_out, alu_1_d2);
  nand nand_194 (nand_194_out, alu_1_nzero, d_ff_6_q);
  nand nand_195 (nand_195_out, nand_187_out, alu_1_d3);
  nand nand_196 (nand_196_out, alu_1_nzero, alu_1_d0);
  nand nand_197 (nand_197_out, nand_187_out, d_ff_3_q);
  nand nand_198 (nand_198_out, alu_1_nzero, alu_1_d1);
  nand nand_199 (nand_199_out, nand_187_out, d_ff_4_q);
  nand nand_200 (nand_200_out, alu_1_nzero, alu_1_d2);
  nand nand_201 (nand_201_out, nand_187_out, d_ff_5_q);
  nand nand_202 (nand_202_out, alu_1_nzero, alu_1_d3);
  nand nand_203 (nand_203_out, nand_187_out, d_ff_6_q);
  nand nand_204 (nand_204_out[0], nand_188_out, nand_189_out);
  nand nand_205 (nand_204_out[1], nand_190_out, nand_191_out);
  nand nand_206 (nand_204_out[2], nand_192_out, nand_193_out);
  nand nand_207 (nand_204_out[3], nand_194_out, nand_195_out);
  nand nand_208 (nand_204_out[4], nand_196_out, nand_197_out);
  nand nand_209 (nand_204_out[5], nand_198_out, nand_199_out);
  nand nand_210 (nand_204_out[6], nand_200_out, nand_201_out);
  nand nand_211 (nand_204_out[7], nand_202_out, nand_203_out);
  nand nand_212 (nand_212_out, T4, BitALU_q);
  nand nand_213 (nand_213_out, T2, BitALU_q);
  nand nand_214 (nand_214_out, alu_1_d0, alu_1_d0);
  nand nand_215 (nand_215_out, alu_1_d1, alu_1_d1);
  nand nand_216 (nand_216_out, alu_1_d2, alu_1_d2);
  nand nand_217 (nand_217_out, alu_1_d3, alu_1_d3);
  nand nand_218 (nand_218_out, nand_212_out, nand_212_out);
  nand nand_219 (nand_219_out, nand_213_out, nand_213_out);
  and9 and9_2 (
    .in_1(d_ff_3_qn), .in_2(d_ff_4_qn), .in_3(d_ff_5_qn), .in_4(d_ff_6_qn), .in_5(nand_214_out),
    .in_6(nand_215_out), .in_7(nand_216_out), .in_8(nand_217_out), .in_9(BitALU_q), .out_10(and9_2_out_10));

  // Notes on the sheet:
  //   NEDONAND LITE. Designed by Shaos in January-March 2016. Released as PUBLIC DOMAIN. Enjoy!
  //   contents of rom_1 (hex, n*v repeats v):
  //   40 89 a9 38 a1 99 79 91 76 76 80 0 b9
  //   /A=n
  //   A=n
  //   NOP
  //   /NOP
  //   /ALU
  //   ALU
  //   R1=R2
  //   Target
  //   invert
  //   RET/RST n
  //   /R=R
  //   HALT
  //   Source
  //   ALU
  //   ADI/SBI
  //   src=A
  //   ALU
  //   ZERO
endmodule

module test_hello (
  input  nRESET,
  output CLK1,
  output nCLK1,
  output CLK2,
  output nCLK2,
  output T1,
  output nT1,
  output T2,
  output nT2,
  output T3,
  output nT3,
  output T4,
  output nT4
);

  wire clock_1_out, dmux8_1_o0, dmux8_1_o1, dmux8_1_o2, dmux8_1_o3, dmux8_1_o4, dmux8_1_o5, dmux8_1_o6,
       dmux8_1_o7, halfadder_1_cout, halfadder_1_dout, halfadder_2_cout, halfadder_2_dout, halfadder_3_cout,
       halfadder_3_dout, halfadder_4_cout, halfadder_4_dout, halfadder_5_cout, halfadder_5_dout,
       halfadder_6_cout, halfadder_6_dout, halfadder_7_cout, halfadder_7_dout, halfadder_8_cout,
       halfadder_8_dout, halfadder_9_cout, halfadder_9_dout, halfadder_10_cout, halfadder_10_dout,
       halfadder_11_dout, halfadder_12_cout, halfadder_12_dout, nand_1_out, nand_2_out, nand_3_out,
       nand_4_out, nand_5_out, nand_6_out, nand_7_out, nand_8_out, nand_9_out, nand_10_out, nand_11_out,
       nand_12_out, nand_13_out, nand_14_out, nand_15_out, nand_16_out, nand_17_out, nand_18_out,
       nand_19_out, nand_20_out, nand_21_out, nand_22_out, nand_23_out, nand_24_out, nand_25_out,
       nand_26_out, nand_27_out, nand_28_out, nand_29_out, nand_30_out, nand_31_out, nand_32_out,
       nand_33_out, nand_34_out, nand_35_out, nand_36_out, nand_37_out, nand_38_out, nand_47_out,
       nand_48_out, nand_49_out, nand_50_out, nand_51_out, nand_52_out, nand_53_out, nand_54_out,
       nand_55_out, nand_56_out, nand_57_out, nand_58_out, nand_59_out, nand_60_out, nand_61_out,
       nand_62_out, nand_63_out, nand_64_out, nand_65_out, nand_74_out, nand_75_out, nand_76_out,
       nand_77_out, nand_78_out, nand_79_out, nand_80_out, nand_81_out, nand_82_out, nand_83_out,
       nand_84_out, nand_85_out, nand_86_out, nand_87_out, nand_88_out, nand_89_out, nand_90_out,
       nand_91_out, nand_92_out, nand_93_out, s_r_ff_1_q, s_r_ff_2_q, xor_1_out, xor_2_out, xor_3_out;
  wire [2:0] rom_1_data_3;
  wire [3:0] rom_1_data_2;
  wire [3:3] rom_1_data;
  wire [7:0] multiplexer_1_out, multiplexer_2_out, nand_66_out, not_1_out, Reg_A_q, Reg_B_q, Reg_C_q,
       Reg_D_q, Reg_E_q, Reg_F_P8_q, Reg_T_q;
  wire [10:0] PC8_q;

  Clock clock_1 (.out(clock_1_out));
  nand nand_1 (nand_1_out, halfadder_12_cout, s_r_ff_1_q);
  nand nand_2 (nand_2_out, clock_1_out, clock_1_out);
  nand nand_3 (nand_3_out, s_r_ff_2_q, s_r_ff_2_q);
  nand nand_4 (nand_4_out, nand_1_out, nand_1_out);
  halfadder halfadder_1 (.A(nand_4_out), .B(PC8_q[0]), .DOUT(halfadder_1_dout), .COUT(halfadder_1_cout));
  halfadder halfadder_2 (.A(halfadder_1_cout), .B(PC8_q[1]), .DOUT(halfadder_2_dout), .COUT(halfadder_2_cout));
  halfadder halfadder_3 (.A(halfadder_2_cout), .B(PC8_q[2]), .DOUT(halfadder_3_dout), .COUT(halfadder_3_cout));
  halfadder halfadder_4 (.A(halfadder_3_cout), .B(PC8_q[3]), .DOUT(halfadder_4_dout), .COUT(halfadder_4_cout));
  halfadder halfadder_5 (.A(halfadder_4_cout), .B(PC8_q[4]), .DOUT(halfadder_5_dout), .COUT(halfadder_5_cout));
  halfadder halfadder_6 (.A(halfadder_5_cout), .B(PC8_q[5]), .DOUT(halfadder_6_dout), .COUT(halfadder_6_cout));
  halfadder halfadder_7 (.A(halfadder_6_cout), .B(PC8_q[6]), .DOUT(halfadder_7_dout), .COUT(halfadder_7_cout));
  halfadder halfadder_8 (.A(halfadder_7_cout), .B(PC8_q[7]), .DOUT(halfadder_8_dout), .COUT(halfadder_8_cout));
  halfadder halfadder_9 (.A(halfadder_8_cout), .B(PC8_q[8]), .DOUT(halfadder_9_dout), .COUT(halfadder_9_cout));
  halfadder halfadder_10 (.A(halfadder_9_cout), .B(PC8_q[9]), .DOUT(halfadder_10_dout), .COUT(halfadder_10_cout));
  halfadder halfadder_11 (.A(halfadder_10_cout), .B(PC8_q[10]), .DOUT(halfadder_11_dout));  // open: COUT
  nand nand_5 (nand_5_out, nand_3_out, multiplexer_2_out[0]);
  nand nand_6 (nand_6_out, s_r_ff_2_q, halfadder_1_dout);
  nand nand_7 (nand_7_out, nand_3_out, multiplexer_2_out[1]);
  nand nand_8 (nand_8_out, s_r_ff_2_q, halfadder_2_dout);
  nand nand_9 (nand_9_out, nand_3_out, multiplexer_2_out[2]);
  nand nand_10 (nand_10_out, s_r_ff_2_q, halfadder_3_dout);
  nand nand_11 (nand_11_out, nand_3_out, multiplexer_2_out[3]);
  nand nand_12 (nand_12_out, s_r_ff_2_q, halfadder_4_dout);
  nand nand_13 (nand_13_out, nand_3_out, multiplexer_2_out[4]);
  nand nand_14 (nand_14_out, s_r_ff_2_q, halfadder_5_dout);
  nand nand_15 (nand_15_out, nand_3_out, multiplexer_2_out[5]);
  nand nand_16 (nand_16_out, s_r_ff_2_q, halfadder_6_dout);
  nand nand_17 (nand_17_out, nand_3_out, multiplexer_2_out[6]);
  nand nand_18 (nand_18_out, s_r_ff_2_q, halfadder_7_dout);
  nand nand_19 (nand_19_out, nand_3_out, multiplexer_2_out[7]);
  nand nand_20 (nand_20_out, s_r_ff_2_q, halfadder_8_dout);
  nand nand_21 (nand_21_out, nand_3_out, Reg_F_P8_q[0]);
  nand nand_22 (nand_22_out, s_r_ff_2_q, halfadder_9_dout);
  nand nand_23 (nand_23_out, nand_3_out, Reg_F_P8_q[1]);
  nand nand_24 (nand_24_out, s_r_ff_2_q, halfadder_10_dout);
  nand nand_25 (nand_25_out, nand_3_out, Reg_F_P8_q[2]);
  nand nand_26 (nand_26_out, s_r_ff_2_q, halfadder_11_dout);
  nand nand_27 (nand_27_out, nRESET, nRESET);
  halfadder halfadder_12 (.A(CLK1), .B(CLK2), .DOUT(halfadder_12_dout), .COUT(halfadder_12_cout));
  nand nand_28 (nand_28_out, nand_5_out, nand_6_out);
  nand nand_29 (nand_29_out, nand_7_out, nand_8_out);
  nand nand_30 (nand_30_out, nand_9_out, nand_10_out);
  nand nand_31 (nand_31_out, nand_11_out, nand_12_out);
  nand nand_32 (nand_32_out, nand_13_out, nand_14_out);
  nand nand_33 (nand_33_out, nand_15_out, nand_16_out);
  nand nand_34 (nand_34_out, nand_17_out, nand_18_out);
  nand nand_35 (nand_35_out, nand_19_out, nand_20_out);
  nand nand_36 (nand_36_out, nand_21_out, nand_22_out);
  nand nand_37 (nand_37_out, nand_23_out, nand_24_out);
  nand nand_38 (nand_38_out, nand_25_out, nand_26_out);
  D_Flip_Flop d_ff_1 (.clk(clock_1_out), .D(nCLK1), .Q(CLK1), .Qn(nCLK1), .reset(nand_27_out));  // open: preset, en
  D_Flip_Flop d_ff_2 (
    .clk(clock_1_out), .D(halfadder_12_dout), .Q(CLK2), .Qn(nCLK2), .reset(nand_27_out));  // open: preset, en
  D_Flip_Flop PC0 (.clk(nT4), .D(nand_28_out), .Q(PC8_q[0]), .reset(nand_27_out));  // open: Qn, preset, en
  D_Flip_Flop PC1 (.clk(nT4), .D(nand_29_out), .Q(PC8_q[1]), .reset(nand_27_out));  // open: Qn, preset, en
  D_Flip_Flop PC2 (.clk(nT4), .D(nand_30_out), .Q(PC8_q[2]), .reset(nand_27_out));  // open: Qn, preset, en
  D_Flip_Flop PC3 (.clk(nT4), .D(nand_31_out), .Q(PC8_q[3]), .reset(nand_27_out));  // open: Qn, preset, en
  D_Flip_Flop PC4 (.clk(nT4), .D(nand_32_out), .Q(PC8_q[4]), .reset(nand_27_out));  // open: Qn, preset, en
  D_Flip_Flop PC5 (.clk(nT4), .D(nand_33_out), .Q(PC8_q[5]), .reset(nand_27_out));  // open: Qn, preset, en
  D_Flip_Flop PC6 (.clk(nT4), .D(nand_34_out), .Q(PC8_q[6]), .reset(nand_27_out));  // open: Qn, preset, en
  D_Flip_Flop PC7 (.clk(nT4), .D(nand_35_out), .Q(PC8_q[7]), .reset(nand_27_out));  // open: Qn, preset, en
  D_Flip_Flop PC8 (.clk(nT4), .D(nand_36_out), .Q(PC8_q[8]), .reset(nand_27_out));  // open: Qn, preset, en
  D_Flip_Flop PC9 (.clk(nT4), .D(nand_37_out), .Q(PC8_q[9]), .reset(nand_27_out));  // open: Qn, preset, en
  D_Flip_Flop PC10 (.clk(nT4), .D(nand_38_out), .Q(PC8_q[10]), .reset(nand_27_out));  // open: Qn, preset, en
  nand nand_39 (nT1, nCLK1, nCLK2);
  nand nand_40 (nT2, nCLK2, CLK1);
  nand nand_41 (nT3, nCLK1, CLK2);
  nand nand_42 (nT4, CLK2, CLK1);
  nand nand_43 (T1, nT1, nT1);
  nand nand_44 (T2, nT2, nT2);
  nand nand_45 (T3, nT3, nT3);
  nand nand_46 (T4, nT4, nT4);
  Hex_Digit_Display hex_digit_display_1 (.value(PC8_q[7:4]));  // open: dp
  Hex_Digit_Display hex_digit_display_2 (.value({1'b0, PC8_q[10:8]}));  // open: dp
  Hex_Digit_Display hex_digit_display_3 (.value(rom_1_data_2));  // open: dp
  S_R_Flip_Flop s_r_ff_1 (.S(T2), .clk(nand_2_out), .R(1'b0), .Q(s_r_ff_1_q));  // open: Qn, preset, reset, en
  S_R_Flip_Flop s_r_ff_2 (.S(T2), .clk(nand_2_out), .R(dmux8_1_o7), .Q(s_r_ff_2_q));  // open: Qn, preset, reset, en
  LED led_1 (.in(T2));
  LED led_2 (.in(T1));
  ROM #(.addrWidth(11)) rom_1 (.addr(PC8_q), .data({rom_1_data_2, rom_1_data[3], rom_1_data_3}));  // open: sel
  Hex_Digit_Display hex_digit_display_4 (.value(PC8_q[3:0]));  // open: dp
  Hex_Digit_Display hex_digit_display_5 (.value({rom_1_data[3], rom_1_data_3}));  // open: dp
  LED led_3 (.in(T4));
  LED led_4 (.in(T3));
  nand nand_47 (nand_47_out, rom_1_data_2[2], rom_1_data_2[3]);
  nand nand_48 (nand_48_out, rom_1_data_2[3], rom_1_data_2[3]);
  nand nand_49 (nand_49_out, nand_48_out, rom_1_data_3[0]);
  nand nand_50 (nand_50_out, rom_1_data_2[3], multiplexer_2_out[0]);
  nand nand_51 (nand_51_out, nand_48_out, rom_1_data_3[1]);
  nand nand_52 (nand_52_out, rom_1_data_2[3], multiplexer_2_out[1]);
  nand nand_53 (nand_53_out, nand_48_out, rom_1_data_3[2]);
  nand nand_54 (nand_54_out, rom_1_data_2[3], multiplexer_2_out[2]);
  nand nand_55 (nand_55_out, nand_48_out, rom_1_data[3]);
  nand nand_56 (nand_56_out, rom_1_data_2[3], multiplexer_2_out[3]);
  nand nand_57 (nand_57_out, nand_48_out, rom_1_data_2[0]);
  nand nand_58 (nand_58_out, rom_1_data_2[3], multiplexer_2_out[4]);
  nand nand_59 (nand_59_out, nand_48_out, rom_1_data_2[1]);
  nand nand_60 (nand_60_out, rom_1_data_2[3], multiplexer_2_out[5]);
  nand nand_61 (nand_61_out, nand_48_out, rom_1_data_2[2]);
  nand nand_62 (nand_62_out, rom_1_data_2[3], multiplexer_2_out[6]);
  nand nand_63 (nand_63_out, nand_48_out, rom_1_data_2[3]);
  nand nand_64 (nand_64_out, rom_1_data_2[3], multiplexer_2_out[7]);
  \xor  xor_1 (.A(rom_1_data_3[0]), .B(rom_1_data[3]), .OUT(xor_1_out));
  \xor  xor_2 (.A(rom_1_data_3[1]), .B(rom_1_data_2[0]), .OUT(xor_2_out));
  \xor  xor_3 (.A(rom_1_data_3[2]), .B(rom_1_data_2[1]), .OUT(xor_3_out));
  nand nand_65 (nand_65_out, nand_47_out, nand_47_out);
  nand nand_66 (nand_66_out[0], nand_49_out, nand_50_out);
  nand nand_67 (nand_66_out[1], nand_51_out, nand_52_out);
  nand nand_68 (nand_66_out[2], nand_53_out, nand_54_out);
  nand nand_69 (nand_66_out[3], nand_55_out, nand_56_out);
  nand nand_70 (nand_66_out[4], nand_57_out, nand_58_out);
  nand nand_71 (nand_66_out[5], nand_59_out, nand_60_out);
  nand nand_72 (nand_66_out[6], nand_61_out, nand_62_out);
  nand nand_73 (nand_66_out[7], nand_63_out, nand_64_out);
  nand nand_74 (nand_74_out, xor_1_out, xor_1_out);
  nand nand_75 (nand_75_out, xor_2_out, xor_2_out);
  nand nand_76 (nand_76_out, xor_3_out, xor_3_out);
  nand nand_77 (nand_77_out, rom_1_data_2[2], rom_1_data_2[2]);
  nand nand_78 (nand_78_out, rom_1_data_2[3], nand_77_out);
  nand nand_79 (nand_79_out, rom_1_data[3], rom_1_data_2[3]);
  nand nand_80 (nand_80_out, rom_1_data_2[0], rom_1_data_2[3]);
  nand nand_81 (nand_81_out, rom_1_data_2[1], rom_1_data_2[3]);
  nand nand_82 (nand_82_out, T4, nand_47_out);
  nand nand_83 (nand_83_out, nand_74_out, nand_75_out);
  nand nand_84 (nand_84_out, nand_78_out, nand_78_out);
  nand nand_85 (nand_85_out, rom_1_data_2[3], nand_79_out);
  nand nand_86 (nand_86_out, nand_80_out, nand_80_out);
  nand nand_87 (nand_87_out, nand_81_out, nand_81_out);
  nand nand_88 (nand_88_out, nand_82_out, nand_82_out);
  nand nand_89 (nand_89_out, nand_83_out, nand_83_out);
  dmux8 dmux8_1 (
    .A0(nand_85_out), .A1(nand_86_out), .A2(nand_87_out), .IN(nand_88_out), .O0(dmux8_1_o0), .O1(dmux8_1_o1),
    .O2(dmux8_1_o2), .O3(dmux8_1_o3), .O4(dmux8_1_o4), .O5(dmux8_1_o5), .O6(dmux8_1_o6), .O7(dmux8_1_o7));
  nand nand_90 (nand_90_out, nand_89_out, nand_76_out);
  nand nand_91 (nand_91_out, nand_90_out, nand_90_out);
  nand nand_92 (nand_92_out, nand_91_out, nand_84_out);
  nand nand_93 (nand_93_out, nand_92_out, nand_92_out);
  Register #(.trigger("high")) Reg_A (.D(nand_66_out), .Q(Reg_A_q), .clk(dmux8_1_o1));  // open: en, clr
  Register #(.trigger("high")) Reg_B (.D(nand_66_out), .Q(Reg_B_q), .clk(dmux8_1_o2));  // open: en, clr
  Register #(.trigger("high")) Reg_C (.D(nand_66_out), .Q(Reg_C_q), .clk(dmux8_1_o3));  // open: en, clr
  Register #(.trigger("high")) Reg_D (.D(nand_66_out), .Q(Reg_D_q), .clk(dmux8_1_o4));  // open: en, clr
  Register #(.trigger("high")) Reg_E (.D(nand_66_out), .Q(Reg_E_q), .clk(dmux8_1_o5));  // open: en, clr
  D_Flip_Flop #(.trigger("high")) Reg_F_S (
    .clk(dmux8_1_o6), .D(nand_66_out[7]), .Q(Reg_F_P8_q[7]));  // open: Qn, preset, en, reset
  D_Flip_Flop #(.trigger("high")) Reg_F_Z (
    .clk(dmux8_1_o6), .D(nand_66_out[6]), .Q(Reg_F_P8_q[6]));  // open: Qn, preset, en, reset
  D_Flip_Flop #(.trigger("high")) Reg_F_V (
    .clk(dmux8_1_o6), .D(nand_66_out[5]), .Q(Reg_F_P8_q[5]));  // open: Qn, preset, en, reset
  D_Flip_Flop #(.trigger("high")) Reg_F_C (
    .clk(dmux8_1_o6), .D(nand_66_out[4]), .Q(Reg_F_P8_q[4]));  // open: Qn, preset, en, reset
  D_Flip_Flop #(.trigger("high")) Reg_F_H (
    .clk(dmux8_1_o6), .D(nand_66_out[3]), .Q(Reg_F_P8_q[3]));  // open: Qn, preset, en, reset
  D_Flip_Flop #(.trigger("high")) Reg_F_P10 (
    .clk(dmux8_1_o6), .D(nand_66_out[2]), .Q(Reg_F_P8_q[2]));  // open: Qn, preset, en, reset
  D_Flip_Flop #(.trigger("high")) Reg_F_P9 (
    .clk(dmux8_1_o6), .D(nand_66_out[1]), .Q(Reg_F_P8_q[1]));  // open: Qn, preset, en, reset
  D_Flip_Flop #(.trigger("high")) Reg_F_P8 (
    .clk(dmux8_1_o6), .D(nand_66_out[0]), .Q(Reg_F_P8_q[0]));  // open: Qn, preset, en, reset
  _7_Segment_Display u_7_segment_display_1 (
    .g(Reg_A_q[6]), .f(Reg_A_q[5]), .a(Reg_A_q[0]), .b(Reg_A_q[1]), .e(Reg_A_q[4]), .d(Reg_A_q[3]),
    .c(Reg_A_q[2]), .dp(Reg_A_q[7]));
  _7_Segment_Display u_7_segment_display_2 (
    .g(Reg_B_q[6]), .f(Reg_B_q[5]), .a(Reg_B_q[0]), .b(Reg_B_q[1]), .e(Reg_B_q[4]), .d(Reg_B_q[3]),
    .c(Reg_B_q[2]), .dp(Reg_B_q[7]));
  Multiplexer #(.select(3), .width(8)) multiplexer_1 (
    .in0({8{1'b0}}), .in1(Reg_A_q), .in2(Reg_B_q), .in3(Reg_C_q), .in4(Reg_D_q), .in5(Reg_E_q),
    .in6(Reg_F_P8_q), .in7(PC8_q[7:0]), .out(multiplexer_1_out), .sel(rom_1_data_3));  // open: en
  _7_Segment_Display u_7_segment_display_3 (
    .g(Reg_C_q[6]), .f(Reg_C_q[5]), .a(Reg_C_q[0]), .b(Reg_C_q[1]), .e(Reg_C_q[4]), .d(Reg_C_q[3]),
    .c(Reg_C_q[2]), .dp(Reg_C_q[7]));
  Register #(.trigger("high")) Reg_T (.D(multiplexer_1_out), .Q(Reg_T_q), .clk(T3));  // open: en, clr
  _7_Segment_Display u_7_segment_display_4 (
    .g(Reg_D_q[6]), .f(Reg_D_q[5]), .a(Reg_D_q[0]), .b(Reg_D_q[1]), .e(Reg_D_q[4]), .d(Reg_D_q[3]),
    .c(Reg_D_q[2]), .dp(Reg_D_q[7]));
  Multiplexer #(.width(8)) multiplexer_2 (
    .in0(Reg_T_q), .in1(not_1_out), .out(multiplexer_2_out), .sel(nand_93_out));  // open: en
  assign not_1_out = ~Reg_T_q;  // NOT_Gate not_1, 8 bits wide
  _7_Segment_Display u_7_segment_display_5 (
    .g(Reg_E_q[6]), .f(Reg_E_q[5]), .a(Reg_E_q[0]), .b(Reg_E_q[1]), .e(Reg_E_q[4]), .d(Reg_E_q[3]),
    .c(Reg_E_q[2]), .dp(Reg_E_q[7]));

  // Notes on the sheet:
  //   contents of rom_1 (hex, n*v repeats v):
  //   40 89 a9 38 a1 99 79 91 76 76 88 b9
  //   A=n
  //   /ALU
  //   ALU
  //   /A=n
  //   R1=R2
  //   Target
  //   RST n
  //   R=~R
  //   Source
endmodule

module nandology (
  input  NOT,
  input  AND,
  input  in_3,
  input  OR,
  input  in_5,
  input  in_6,
  input  in_7,
  input  MUX,
  input  in_9,
  input  in_10,
  output out_11,
  output out_12,
  output out_13,
  output out_14,
  output out_15
);

  wire nand_2_out, nand_3_out, nand_4_out, nand_5_out, nand_8_out, nand_9_out, nand_10_out, nand_12_out,
       nand_13_out;

  nand nand_1 (out_11, NOT, NOT);
  nand nand_2 (nand_2_out, AND, in_3);
  nand nand_3 (nand_3_out, OR, OR);
  nand nand_4 (nand_4_out, in_5, in_5);
  nand nand_5 (nand_5_out, in_6, in_7);
  nand nand_6 (out_12, nand_2_out, nand_2_out);
  nand nand_7 (out_13, nand_3_out, nand_4_out);
  nand nand_8 (nand_8_out, in_6, nand_5_out);
  nand nand_9 (nand_9_out, nand_5_out, in_7);
  nand nand_10 (nand_10_out, MUX, MUX);
  nand nand_11 (out_14, nand_8_out, nand_9_out);
  nand nand_12 (nand_12_out, nand_10_out, in_9);
  nand nand_13 (nand_13_out, MUX, in_10);
  nand nand_14 (out_15, nand_12_out, nand_13_out);

  // Notes on the sheet:
  //   XOR
endmodule

module dtrig (
  input  D,
  input  C,
  output Q,
  output nQ
);

  wire nand_1_out, nand_2_out;

  nand nand_1 (nand_1_out, D, C);
  nand nand_2 (nand_2_out, nand_1_out, C);
  nand nand_3 (Q, nQ, nand_1_out);
  nand nand_4 (nQ, Q, nand_2_out);
endmodule

module dtrig2 (
  input  D,
  input  C,
  input  nC,
  output Q,
  output nQ
);

  wire dtrig_1_q;

  dtrig dtrig_1 (.D(D), .C(nC), .Q(dtrig_1_q));  // open: nQ
  dtrig dtrig_2 (.D(dtrig_1_q), .C(C), .Q(Q), .nQ(nQ));
endmodule

module dtrig2r (
  input  D,
  input  C,
  input  nR,
  output Q,
  output nQ
);

  wire nand_1_out, nand_2_out, nand_3_out, nand_4_out, nand_5_out, nand_6_out, nand_7_out, nand_9_out,
       nand_10_out, nand_11_out;

  nand nand_1 (nand_1_out, C, C);
  nand nand_2 (nand_2_out, D, nand_1_out);
  nand nand_3 (nand_3_out, nand_2_out, nand_1_out);
  nand nand_4 (nand_4_out, nand_5_out, nand_2_out);
  nand nand_5 (nand_5_out, nand_4_out, nand_3_out);
  nand nand_6 (nand_6_out, nand_1_out, nand_1_out);
  nand nand_7 (nand_7_out, nand_4_out, nand_6_out);
  nand nand_8 (Q, nQ, nand_7_out);
  nand nand_9 (nand_9_out, nand_7_out, nand_6_out);
  nand nand_10 (nand_10_out, Q, nand_9_out);
  nand nand_11 (nand_11_out, nand_10_out, nand_10_out);
  nand nand_12 (nQ, nand_11_out, nR);
endmodule

module dtrig2rs (
  input  nS,
  input  D,
  input  C,
  input  nR,
  output Q,
  output nQ
);

  wire nand_1_out, nand_2_out, nand_3_out, nand_4_out, nand_5_out, nand_6_out, nand_7_out, nand_8_out,
       nand_9_out, nand_10_out, nand_11_out, nand_12_out, nand_13_out, nand_14_out, nand_15_out, nand_16_out;

  nand nand_1 (nand_1_out, C, C);
  nand nand_2 (nand_2_out, D, nand_1_out);
  nand nand_3 (nand_3_out, nand_2_out, nand_1_out);
  nand nand_4 (nand_4_out, nand_2_out, nand_9_out);
  nand nand_5 (nand_5_out, nand_8_out, nand_3_out);
  nand nand_6 (nand_6_out, nand_4_out, nand_4_out);
  nand nand_7 (nand_7_out, nand_5_out, nand_5_out);
  nand nand_8 (nand_8_out, nS, nand_6_out);
  nand nand_9 (nand_9_out, nand_7_out, nR);
  nand nand_10 (nand_10_out, nand_1_out, nand_1_out);
  nand nand_11 (nand_11_out, nand_8_out, nand_10_out);
  nand nand_12 (nand_12_out, nand_11_out, nand_10_out);
  nand nand_13 (nand_13_out, nand_11_out, nQ);
  nand nand_14 (nand_14_out, Q, nand_12_out);
  nand nand_15 (nand_15_out, nand_13_out, nand_13_out);
  nand nand_16 (nand_16_out, nand_14_out, nand_14_out);
  nand nand_17 (Q, nS, nand_15_out);
  nand nand_18 (nQ, nand_16_out, nR);
endmodule

module rstrig (
  input  nS,
  input  nR,
  output Q,
  output nQ
);

  nand nand_1 (Q, nS, nQ);
  nand nand_2 (nQ, Q, nR);
endmodule

module mux8 (
  input  A0,
  input  A1,
  input  A2,
  input  D0,
  input  D1,
  input  D2,
  input  D3,
  input  D4,
  input  D5,
  input  D6,
  input  D7,
  output OUT
);

  wire nand_1_out, nand_2_out, nand_3_out, nand_4_out, nand_5_out, nand_6_out, nand_7_out, nand_8_out,
       nand_9_out, nand_10_out, nand_11_out, nand_12_out, nand_13_out, nand_14_out, nand_15_out, nand_16_out,
       nand_17_out, nand_18_out, nand_19_out, nand_20_out, nand_21_out, nand_22_out, nand_23_out;

  nand nand_1 (nand_1_out, A0, A0);
  nand nand_2 (nand_2_out, nand_1_out, D0);
  nand nand_3 (nand_3_out, A0, D1);
  nand nand_4 (nand_4_out, nand_1_out, D2);
  nand nand_5 (nand_5_out, A0, D3);
  nand nand_6 (nand_6_out, nand_1_out, D4);
  nand nand_7 (nand_7_out, A0, D5);
  nand nand_8 (nand_8_out, nand_1_out, D6);
  nand nand_9 (nand_9_out, A0, D7);
  nand nand_10 (nand_10_out, nand_2_out, nand_3_out);
  nand nand_11 (nand_11_out, nand_4_out, nand_5_out);
  nand nand_12 (nand_12_out, nand_6_out, nand_7_out);
  nand nand_13 (nand_13_out, nand_8_out, nand_9_out);
  nand nand_14 (nand_14_out, A1, A1);
  nand nand_15 (nand_15_out, nand_14_out, nand_10_out);
  nand nand_16 (nand_16_out, A1, nand_11_out);
  nand nand_17 (nand_17_out, nand_14_out, nand_12_out);
  nand nand_18 (nand_18_out, A1, nand_13_out);
  nand nand_19 (nand_19_out, nand_15_out, nand_16_out);
  nand nand_20 (nand_20_out, nand_17_out, nand_18_out);
  nand nand_21 (nand_21_out, A2, A2);
  nand nand_22 (nand_22_out, nand_21_out, nand_19_out);
  nand nand_23 (nand_23_out, A2, nand_20_out);
  nand nand_24 (OUT, nand_22_out, nand_23_out);
endmodule

module mux2 (
  input  S,
  input  D0,
  input  D1,
  output OUT
);

  wire nand_1_out, nand_2_out, nand_3_out;

  nand nand_1 (nand_1_out, S, S);
  nand nand_2 (nand_2_out, nand_1_out, D0);
  nand nand_3 (nand_3_out, S, D1);
  nand nand_4 (OUT, nand_2_out, nand_3_out);
endmodule

module dmux8 (
  input  A0,
  input  A1,
  input  A2,
  input  IN,
  output O0,
  output O1,
  output O2,
  output O3,
  output O4,
  output O5,
  output O6,
  output O7
);

  wire nand_1_out, nand_2_out, nand_3_out, nand_4_out, nand_5_out, nand_6_out, nand_7_out, nand_8_out,
       nand_9_out, nand_10_out, nand_11_out, nand_12_out, nand_13_out, nand_14_out, nand_15_out, nand_16_out,
       nand_17_out, nand_18_out, nand_19_out, nand_20_out, nand_21_out, nand_22_out, nand_23_out;

  nand nand_1 (nand_1_out, A2, A2);
  nand nand_2 (nand_2_out, nand_1_out, IN);
  nand nand_3 (nand_3_out, IN, A2);
  nand nand_4 (nand_4_out, nand_2_out, nand_2_out);
  nand nand_5 (nand_5_out, nand_3_out, nand_3_out);
  nand nand_6 (nand_6_out, A1, A1);
  nand nand_7 (nand_7_out, nand_6_out, nand_4_out);
  nand nand_8 (nand_8_out, nand_4_out, A1);
  nand nand_9 (nand_9_out, nand_6_out, nand_5_out);
  nand nand_10 (nand_10_out, nand_5_out, A1);
  nand nand_11 (nand_11_out, A0, A0);
  nand nand_12 (nand_12_out, nand_7_out, nand_7_out);
  nand nand_13 (nand_13_out, nand_8_out, nand_8_out);
  nand nand_14 (nand_14_out, nand_9_out, nand_9_out);
  nand nand_15 (nand_15_out, nand_10_out, nand_10_out);
  nand nand_16 (nand_16_out, nand_11_out, nand_12_out);
  nand nand_17 (nand_17_out, nand_12_out, A0);
  nand nand_18 (nand_18_out, nand_11_out, nand_13_out);
  nand nand_19 (nand_19_out, nand_13_out, A0);
  nand nand_20 (nand_20_out, nand_11_out, nand_14_out);
  nand nand_21 (nand_21_out, nand_14_out, A0);
  nand nand_22 (nand_22_out, nand_11_out, nand_15_out);
  nand nand_23 (nand_23_out, nand_15_out, A0);
  nand nand_24 (O0, nand_16_out, nand_16_out);
  nand nand_25 (O1, nand_17_out, nand_17_out);
  nand nand_26 (O2, nand_18_out, nand_18_out);
  nand nand_27 (O3, nand_19_out, nand_19_out);
  nand nand_28 (O4, nand_20_out, nand_20_out);
  nand nand_29 (O5, nand_21_out, nand_21_out);
  nand nand_30 (O6, nand_22_out, nand_22_out);
  nand nand_31 (O7, nand_23_out, nand_23_out);
endmodule

module dmux2 (
  input  S,
  input  IN,
  output O0,
  output O1
);

  wire nand_1_out, nand_2_out, nand_3_out;

  nand nand_1 (nand_1_out, S, S);
  nand nand_2 (nand_2_out, nand_1_out, IN);
  nand nand_3 (nand_3_out, IN, S);
  nand nand_4 (O0, nand_2_out, nand_2_out);
  nand nand_5 (O1, nand_3_out, nand_3_out);
endmodule

module dmux2z (
  input  S,
  input  IN,
  output O0,
  output O1
);

  wire nand_1_out, nand_2_out;

  nand nand_1 (nand_1_out, S, S);
  nand nand_2 (nand_2_out, IN, IN);
  nand nand_3 (O0, nand_1_out, nand_2_out);
  nand nand_4 (O1, nand_2_out, S);
endmodule

module \xor  (
  input  A,
  input  B,
  output OUT
);

  wire nand_1_out, nand_2_out, nand_3_out;

  nand nand_1 (nand_1_out, A, B);
  nand nand_2 (nand_2_out, A, nand_1_out);
  nand nand_3 (nand_3_out, nand_1_out, B);
  nand nand_4 (OUT, nand_2_out, nand_3_out);
endmodule

module halfadder (
  input  A,
  input  B,
  output DOUT,
  output COUT
);

  wire nand_1_out, nand_2_out, nand_3_out;

  nand nand_1 (nand_1_out, A, B);
  nand nand_2 (nand_2_out, A, nand_1_out);
  nand nand_3 (nand_3_out, nand_1_out, B);
  nand nand_4 (COUT, nand_1_out, nand_1_out);
  nand nand_5 (DOUT, nand_2_out, nand_3_out);
endmodule

module slice (
  input  O0,
  input  O1,
  input  O2,
  input  A,
  input  B,
  input  C,
  input  H,
  input  L,
  output COUT,
  output DOUT
);

  wire nand_1_out, nand_2_out, nand_3_out, nand_4_out, nand_5_out, nand_6_out, nand_7_out, nand_9_out,
       nand_10_out, nand_11_out, nand_12_out, nand_13_out, nand_14_out, nand_15_out, nand_16_out,
       nand_17_out, nand_18_out, nand_19_out, nand_20_out, nand_21_out, nand_22_out, nand_23_out;

  nand nand_1 (nand_1_out, A, B);
  nand nand_2 (nand_2_out, A, nand_1_out);
  nand nand_3 (nand_3_out, nand_1_out, B);
  nand nand_4 (nand_4_out, nand_2_out, nand_3_out);
  nand nand_5 (nand_5_out, nand_4_out, C);
  nand nand_6 (nand_6_out, nand_4_out, nand_5_out);
  nand nand_7 (nand_7_out, nand_5_out, C);
  nand nand_8 (COUT, nand_1_out, nand_5_out);
  nand nand_9 (nand_9_out, nand_6_out, nand_7_out);
  nand nand_10 (nand_10_out, O0, O0);
  nand nand_11 (nand_11_out, nand_10_out, H);
  nand nand_12 (nand_12_out, O0, L);
  nand nand_13 (nand_13_out, nand_10_out, nand_1_out);
  nand nand_14 (nand_14_out, O0, nand_4_out);
  nand nand_15 (nand_15_out, nand_11_out, nand_12_out);
  nand nand_16 (nand_16_out, nand_13_out, nand_14_out);
  nand nand_17 (nand_17_out, O1, O1);
  nand nand_18 (nand_18_out, nand_17_out, nand_15_out);
  nand nand_19 (nand_19_out, O1, nand_16_out);
  nand nand_20 (nand_20_out, nand_18_out, nand_19_out);
  nand nand_21 (nand_21_out, O2, O2);
  nand nand_22 (nand_22_out, nand_21_out, nand_20_out);
  nand nand_23 (nand_23_out, O2, nand_9_out);
  nand nand_24 (DOUT, nand_22_out, nand_23_out);
endmodule

module alu (
  input  O0,
  input  O1,
  input  O2,
  input  A0,
  input  A1,
  input  A2,
  input  A3,
  input  B0,
  input  B1,
  input  B2,
  input  B3,
  input  C,
  output nZERO,
  output V_prime,
  output C_prime,
  output D0,
  output D1,
  output D2,
  output D3
);

  wire nand_1_out, nand_2_out, nand_3_out, nand_4_out, nand_5_out, nand_6_out, nand_7_out, nand_8_out,
       nand_9_out, nand_10_out, nand_11_out, nand_12_out, nand_14_out, nand_15_out, nand_16_out, nand_17_out,
       nand_18_out, nand_19_out, nand_20_out, nand_21_out, nand_23_out, slice_1_cout, slice_2_cout,
       slice_3_cout, slice_4_cout;

  nand nand_1 (nand_1_out, nand_4_out, C);
  nand nand_2 (nand_2_out, nand_1_out, nand_1_out);
  slice slice_1 (
    .O0(O0), .O1(O1), .O2(O2), .A(A0), .B(B0), .C(nand_2_out), .H(B1), .L(C), .COUT(slice_1_cout), .DOUT(D0));
  slice slice_2 (
    .O0(O0), .O1(O1), .O2(O2), .A(A1), .B(B1), .C(slice_1_cout), .H(B2), .L(B0), .COUT(slice_2_cout),
    .DOUT(D1));
  slice slice_3 (
    .O0(O0), .O1(O1), .O2(O2), .A(A2), .B(B2), .C(slice_2_cout), .H(B3), .L(B1), .COUT(slice_3_cout),
    .DOUT(D2));
  slice slice_4 (
    .O0(O0), .O1(O1), .O2(O2), .A(A3), .B(B3), .C(slice_3_cout), .H(C), .L(B2), .COUT(slice_4_cout), .DOUT(D3));
  nand nand_3 (nand_3_out, O0, O0);
  nand nand_4 (nand_4_out, O1, O2);
  nand nand_5 (nand_5_out, O1, O1);
  nand nand_6 (nand_6_out, O2, O2);
  nand nand_7 (nand_7_out, nand_3_out, B0);
  nand nand_8 (nand_8_out, O0, B3);
  nand nand_9 (nand_9_out, nand_5_out, nand_6_out);
  nand nand_10 (nand_10_out, nand_7_out, nand_8_out);
  nand nand_11 (nand_11_out, O1, nand_6_out);
  nand nand_12 (nand_12_out, nand_9_out, nand_9_out);
  nand nand_13 (nZERO, nand_3_out, nand_12_out);
  nand nand_14 (nand_14_out, slice_3_cout, slice_4_cout);
  nand nand_15 (nand_15_out, nand_12_out, nand_10_out);
  nand nand_16 (nand_16_out, nand_9_out, slice_4_cout);
  nand nand_17 (nand_17_out, slice_3_cout, nand_14_out);
  nand nand_18 (nand_18_out, nand_14_out, slice_4_cout);
  nand nand_19 (nand_19_out, nand_15_out, nand_16_out);
  nand nand_20 (nand_20_out, O2, nand_21_out);
  nand nand_21 (nand_21_out, nand_17_out, nand_18_out);
  nand nand_22 (C_prime, nand_11_out, nand_23_out);
  nand nand_23 (nand_23_out, nand_19_out, nand_19_out);
  nand nand_24 (V_prime, nand_20_out, nand_20_out);
endmodule

module clock (
  input  nRESET,
  input  nLOAD,
  input  COUNT,
  input  D0,
  input  D1,
  input  D2,
  input  D3,
  input  D4,
  input  D5,
  input  D6,
  input  D7,
  input  D8,
  input  D9,
  input  D10,
  output CLK1,
  output nCLK1,
  output CLK2,
  output nCLK2,
  output T1,
  output nT1,
  output T2,
  output nT2,
  output T3,
  output nT3,
  output T4,
  output nT4,
  output P0,
  output P1,
  output P2,
  output P3,
  output P4,
  output P5,
  output P6,
  output P7,
  output P8,
  output P9,
  output P10
);

  wire clock_1_out, nand_1_out, nand_2_out, nand_3_out, nand_4_out, nand_5_out, nand_6_out, nand_7_out,
       nand_8_out, nand_9_out, nand_10_out, nand_11_out, nand_12_out, nand_13_out, nand_14_out, nand_15_out,
       nand_16_out, nand_17_out, nand_18_out, nand_19_out, nand_20_out, nand_21_out, nand_22_out,
       nand_23_out, nand_24_out, nand_25_out, nand_26_out, nand_27_out, nand_28_out, nand_29_out,
       nand_30_out, nand_31_out, nand_32_out, nand_33_out, nand_34_out, nand_35_out, nand_36_out,
       nand_37_out, nand_38_out, nand_39_out, nand_40_out, nand_41_out, nand_42_out, nand_43_out,
       nand_44_out, nand_45_out, nand_46_out, nand_47_out, nand_48_out, nand_49_out, nand_50_out,
       nand_51_out, nand_52_out, nand_53_out, nand_54_out, nand_55_out, nand_56_out, nand_57_out,
       nand_58_out, nand_59_out, nand_60_out, nand_61_out, nand_62_out, nand_63_out, nand_64_out,
       nand_65_out, nand_66_out, nand_67_out, nand_68_out, nand_69_out, nand_70_out, nand_71_out,
       nand_72_out, nand_73_out, nand_74_out, nand_75_out, nand_76_out, nand_77_out, nand_78_out,
       nand_79_out, nand_80_out, nand_81_out, nand_82_out, nand_83_out, nand_84_out, nand_89_out,
       nand_90_out, nand_91_out, nand_92_out, nand_93_out, nand_94_out, nand_95_out, nand_96_out,
       nand_97_out, nand_98_out, nand_99_out;

  nand nand_1 (nand_1_out, nand_12_out, COUNT);
  nand nand_2 (nand_2_out, nand_16_out, nand_16_out);
  nand nand_3 (nand_3_out, nand_17_out, nand_17_out);
  nand nand_4 (nand_4_out, nand_18_out, nand_18_out);
  nand nand_5 (nand_5_out, nand_19_out, nand_19_out);
  nand nand_6 (nand_6_out, nand_20_out, nand_20_out);
  nand nand_7 (nand_7_out, nand_21_out, nand_21_out);
  nand nand_8 (nand_8_out, nand_22_out, nand_22_out);
  nand nand_9 (nand_9_out, nand_23_out, nand_23_out);
  nand nand_10 (nand_10_out, nand_24_out, nand_24_out);
  nand nand_11 (nand_11_out, nand_25_out, nand_25_out);
  nand nand_12 (nand_12_out, nand_14_out, nand_14_out);
  nand nand_13 (nand_13_out, nLOAD, nLOAD);
  nand nand_14 (nand_14_out, CLK1, CLK2);
  nand nand_15 (nand_15_out, nand_1_out, nand_1_out);
  nand nand_16 (nand_16_out, nand_15_out, P0);
  nand nand_17 (nand_17_out, nand_2_out, P1);
  nand nand_18 (nand_18_out, nand_3_out, P2);
  nand nand_19 (nand_19_out, nand_4_out, P3);
  nand nand_20 (nand_20_out, nand_5_out, P4);
  nand nand_21 (nand_21_out, nand_6_out, P5);
  nand nand_22 (nand_22_out, nand_7_out, P6);
  nand nand_23 (nand_23_out, nand_8_out, P7);
  nand nand_24 (nand_24_out, nand_9_out, P8);
  nand nand_25 (nand_25_out, nand_10_out, P9);
  nand nand_26 (nand_26_out, nand_11_out, P10);
  nand nand_27 (nand_27_out, CLK1, nand_14_out);
  nand nand_28 (nand_28_out, nand_14_out, CLK2);
  nand nand_29 (nand_29_out, nand_15_out, nand_16_out);
  nand nand_30 (nand_30_out, nand_16_out, P0);
  nand nand_31 (nand_31_out, nand_2_out, nand_17_out);
  nand nand_32 (nand_32_out, nand_17_out, P1);
  nand nand_33 (nand_33_out, nand_3_out, nand_18_out);
  nand nand_34 (nand_34_out, nand_18_out, P2);
  nand nand_35 (nand_35_out, nand_4_out, nand_19_out);
  nand nand_36 (nand_36_out, nand_19_out, P3);
  nand nand_37 (nand_37_out, nand_5_out, nand_20_out);
  nand nand_38 (nand_38_out, nand_20_out, P4);
  nand nand_39 (nand_39_out, nand_6_out, nand_21_out);
  nand nand_40 (nand_40_out, nand_21_out, P5);
  nand nand_41 (nand_41_out, nand_7_out, nand_22_out);
  nand nand_42 (nand_42_out, nand_22_out, P6);
  nand nand_43 (nand_43_out, nand_8_out, nand_23_out);
  nand nand_44 (nand_44_out, nand_23_out, P7);
  nand nand_45 (nand_45_out, nand_9_out, nand_24_out);
  nand nand_46 (nand_46_out, nand_24_out, P8);
  nand nand_47 (nand_47_out, nand_10_out, nand_25_out);
  nand nand_48 (nand_48_out, nand_25_out, P9);
  nand nand_49 (nand_49_out, nand_11_out, nand_26_out);
  nand nand_50 (nand_50_out, nand_26_out, P10);
  Clock clock_1 (.out(clock_1_out));
  nand nand_51 (nand_51_out, nand_27_out, nand_28_out);
  nand nand_52 (nand_52_out, nand_29_out, nand_30_out);
  nand nand_53 (nand_53_out, nand_31_out, nand_32_out);
  nand nand_54 (nand_54_out, nand_33_out, nand_34_out);
  nand nand_55 (nand_55_out, nand_35_out, nand_36_out);
  nand nand_56 (nand_56_out, nand_37_out, nand_38_out);
  nand nand_57 (nand_57_out, nand_39_out, nand_40_out);
  nand nand_58 (nand_58_out, nand_41_out, nand_42_out);
  nand nand_59 (nand_59_out, nand_43_out, nand_44_out);
  nand nand_60 (nand_60_out, nand_45_out, nand_46_out);
  nand nand_61 (nand_61_out, nand_47_out, nand_48_out);
  nand nand_62 (nand_62_out, nand_49_out, nand_50_out);
  nand nand_63 (nand_63_out, nand_13_out, D0);
  nand nand_64 (nand_64_out, nLOAD, nand_52_out);
  nand nand_65 (nand_65_out, nand_13_out, D1);
  nand nand_66 (nand_66_out, nLOAD, nand_53_out);
  nand nand_67 (nand_67_out, nand_13_out, D2);
  nand nand_68 (nand_68_out, nLOAD, nand_54_out);
  nand nand_69 (nand_69_out, nand_13_out, D3);
  nand nand_70 (nand_70_out, nLOAD, nand_55_out);
  nand nand_71 (nand_71_out, nand_13_out, D4);
  nand nand_72 (nand_72_out, nLOAD, nand_56_out);
  nand nand_73 (nand_73_out, nand_13_out, D5);
  nand nand_74 (nand_74_out, nLOAD, nand_57_out);
  nand nand_75 (nand_75_out, nand_13_out, D6);
  nand nand_76 (nand_76_out, nLOAD, nand_58_out);
  nand nand_77 (nand_77_out, nand_13_out, D7);
  nand nand_78 (nand_78_out, nLOAD, nand_59_out);
  nand nand_79 (nand_79_out, nand_13_out, D8);
  nand nand_80 (nand_80_out, nLOAD, nand_60_out);
  nand nand_81 (nand_81_out, nand_13_out, D9);
  nand nand_82 (nand_82_out, nLOAD, nand_61_out);
  nand nand_83 (nand_83_out, nand_13_out, D10);
  nand nand_84 (nand_84_out, nLOAD, nand_62_out);
  dtrig2rs dtrig2rs_1 (.nS(1'b1), .D(nCLK1), .C(clock_1_out), .nR(nRESET), .Q(CLK1), .nQ(nCLK1));
  dtrig2rs dtrig2rs_2 (.nS(1'b1), .D(nand_51_out), .C(clock_1_out), .nR(nRESET), .Q(CLK2), .nQ(nCLK2));
  nand nand_85 (nT1, nCLK1, nCLK2);
  nand nand_86 (nT2, nCLK2, CLK1);
  nand nand_87 (nT3, nCLK1, CLK2);
  nand nand_88 (nT4, CLK2, CLK1);
  nand nand_89 (nand_89_out, nand_63_out, nand_64_out);
  nand nand_90 (nand_90_out, nand_65_out, nand_66_out);
  nand nand_91 (nand_91_out, nand_67_out, nand_68_out);
  nand nand_92 (nand_92_out, nand_69_out, nand_70_out);
  nand nand_93 (nand_93_out, nand_71_out, nand_72_out);
  nand nand_94 (nand_94_out, nand_73_out, nand_74_out);
  nand nand_95 (nand_95_out, nand_75_out, nand_76_out);
  nand nand_96 (nand_96_out, nand_77_out, nand_78_out);
  nand nand_97 (nand_97_out, nand_79_out, nand_80_out);
  nand nand_98 (nand_98_out, nand_81_out, nand_82_out);
  nand nand_99 (nand_99_out, nand_83_out, nand_84_out);
  nand nand_100 (T1, nT1, nT1);
  nand nand_101 (T2, nT2, nT2);
  nand nand_102 (T3, nT3, nT3);
  nand nand_103 (T4, nT4, nT4);
  dtrig2rs dtrig2rs_3 (.nS(1'b1), .D(nand_89_out), .C(clock_1_out), .nR(nRESET), .Q(P0));  // open: nQ
  dtrig2rs dtrig2rs_4 (.nS(1'b1), .D(nand_90_out), .C(clock_1_out), .nR(nRESET), .Q(P1));  // open: nQ
  dtrig2rs dtrig2rs_5 (.nS(1'b1), .D(nand_91_out), .C(clock_1_out), .nR(nRESET), .Q(P2));  // open: nQ
  dtrig2rs dtrig2rs_6 (.nS(1'b1), .D(nand_92_out), .C(clock_1_out), .nR(nRESET), .Q(P3));  // open: nQ
  dtrig2rs dtrig2rs_7 (.nS(1'b1), .D(nand_93_out), .C(clock_1_out), .nR(nRESET), .Q(P4));  // open: nQ
  dtrig2rs dtrig2rs_8 (.nS(1'b1), .D(nand_94_out), .C(clock_1_out), .nR(nRESET), .Q(P5));  // open: nQ
  dtrig2rs dtrig2rs_9 (.nS(1'b1), .D(nand_95_out), .C(clock_1_out), .nR(nRESET), .Q(P6));  // open: nQ
  dtrig2rs dtrig2rs_10 (.nS(1'b1), .D(nand_96_out), .C(clock_1_out), .nR(nRESET), .Q(P7));  // open: nQ
  dtrig2rs dtrig2rs_11 (.nS(1'b1), .D(nand_97_out), .C(clock_1_out), .nR(nRESET), .Q(P8));  // open: nQ
  dtrig2rs dtrig2rs_12 (.nS(1'b1), .D(nand_98_out), .C(clock_1_out), .nR(nRESET), .Q(P9));  // open: nQ
  dtrig2rs dtrig2rs_13 (.nS(1'b1), .D(nand_99_out), .C(clock_1_out), .nR(nRESET), .Q(P10));  // open: nQ
endmodule

module rom16 (
  input  A0,
  input  A1,
  input  A2,
  input  A3,
  output D0,
  output D1,
  output D2,
  output D3,
  output D4,
  output D5,
  output D6,
  output D7
);

  wire nand_1_out, nand_2_out, nand_3_out, nand_4_out, nand_5_out, nand_6_out, nand_7_out, nand_8_out,
       nand_9_out, nand_10_out, nand_11_out, nand_12_out, nand_13_out, nand_14_out, nand_15_out, nand_16_out,
       nand_17_out, nand_18_out, nand_19_out, nand_20_out, nand_21_out, nand_22_out, nand_23_out,
       nand_24_out, nand_25_out, nand_26_out, nand_27_out, nand_28_out, nand_29_out, nand_30_out,
       nand_31_out, nand_32_out, nand_33_out, nand_34_out, nand_35_out, nand_36_out, pull_resistor_1_node,
       pull_resistor_2_node, pull_resistor_3_node, pull_resistor_4_node, pull_resistor_5_node,
       pull_resistor_6_node, pull_resistor_7_node, pull_resistor_8_node;

  nand nand_1 (nand_1_out, A0, A0);
  nand nand_2 (nand_2_out, A1, A1);
  nand nand_3 (nand_3_out, A2, A2);
  nand nand_4 (nand_4_out, A3, A3);
  nand nand_5 (nand_5_out, nand_1_out, nand_2_out);
  nand nand_6 (nand_6_out, A0, nand_2_out);
  nand nand_7 (nand_7_out, nand_1_out, A1);
  nand nand_8 (nand_8_out, A0, A1);
  nand nand_9 (nand_9_out, nand_3_out, nand_4_out);
  nand nand_10 (nand_10_out, A2, nand_4_out);
  nand nand_11 (nand_11_out, nand_3_out, A3);
  nand nand_12 (nand_12_out, A2, A3);
  nand nand_13 (nand_13_out, nand_5_out, nand_5_out);
  nand nand_14 (nand_14_out, nand_6_out, nand_6_out);
  nand nand_15 (nand_15_out, nand_7_out, nand_7_out);
  nand nand_16 (nand_16_out, nand_8_out, nand_8_out);
  nand nand_17 (nand_17_out, nand_9_out, nand_9_out);
  nand nand_18 (nand_18_out, nand_10_out, nand_10_out);
  nand nand_19 (nand_19_out, nand_11_out, nand_11_out);
  nand nand_20 (nand_20_out, nand_12_out, nand_12_out);
  nand nand_21 (nand_21_out, nand_13_out, nand_17_out);
  nand nand_22 (nand_22_out, nand_14_out, nand_17_out);
  nand nand_23 (nand_23_out, nand_15_out, nand_17_out);
  nand nand_24 (nand_24_out, nand_16_out, nand_17_out);
  nand nand_25 (nand_25_out, nand_13_out, nand_18_out);
  nand nand_26 (nand_26_out, nand_14_out, nand_18_out);
  nand nand_27 (nand_27_out, nand_15_out, nand_18_out);
  nand nand_28 (nand_28_out, nand_16_out, nand_18_out);
  nand nand_29 (nand_29_out, nand_13_out, nand_19_out);
  nand nand_30 (nand_30_out, nand_14_out, nand_19_out);
  nand nand_31 (nand_31_out, nand_15_out, nand_19_out);
  nand nand_32 (nand_32_out, nand_16_out, nand_19_out);
  nand nand_33 (nand_33_out, nand_13_out, nand_20_out);
  nand nand_34 (nand_34_out, nand_14_out, nand_20_out);
  nand nand_35 (nand_35_out, nand_15_out, nand_20_out);
  nand nand_36 (nand_36_out, nand_16_out, nand_20_out);
  Pull_Resistor #(.pull(1)) pull_resistor_1 (.node(pull_resistor_1_node));
  Pull_Resistor #(.pull(1)) pull_resistor_2 (.node(pull_resistor_2_node));
  Pull_Resistor #(.pull(1)) pull_resistor_3 (.node(pull_resistor_3_node));
  Pull_Resistor #(.pull(1)) pull_resistor_4 (.node(pull_resistor_4_node));
  Pull_Resistor #(.pull(1)) pull_resistor_5 (.node(pull_resistor_5_node));
  Pull_Resistor #(.pull(1)) pull_resistor_6 (.node(pull_resistor_6_node));
  Pull_Resistor #(.pull(1)) pull_resistor_7 (.node(pull_resistor_7_node));
  Pull_Resistor #(.pull(1)) pull_resistor_8 (.node(pull_resistor_8_node));
  nand nand_37 (D0, pull_resistor_7_node, pull_resistor_7_node);
  nand nand_38 (D1, pull_resistor_8_node, pull_resistor_8_node);
  nand nand_39 (D2, pull_resistor_5_node, pull_resistor_5_node);
  nand nand_40 (D3, pull_resistor_6_node, pull_resistor_6_node);
  nand nand_41 (D4, pull_resistor_4_node, pull_resistor_4_node);
  nand nand_42 (D5, pull_resistor_3_node, pull_resistor_3_node);
  nand nand_43 (D6, pull_resistor_2_node, pull_resistor_2_node);
  nand nand_44 (D7, pull_resistor_1_node, pull_resistor_1_node);
endmodule

module and9 (
  input  in_1,
  input  in_2,
  input  in_3,
  input  in_4,
  input  in_5,
  input  in_6,
  input  in_7,
  input  in_8,
  input  in_9,
  output out_10
);

  wire nand_1_out, nand_2_out, nand_3_out, nand_4_out, nand_5_out, nand_6_out, nand_7_out, nand_8_out,
       nand_9_out, nand_10_out, nand_11_out, nand_12_out, nand_13_out, nand_14_out, nand_15_out;

  nand nand_1 (nand_1_out, in_1, in_2);
  nand nand_2 (nand_2_out, in_3, in_4);
  nand nand_3 (nand_3_out, in_5, in_6);
  nand nand_4 (nand_4_out, in_7, in_8);
  nand nand_5 (nand_5_out, nand_1_out, nand_1_out);
  nand nand_6 (nand_6_out, nand_2_out, nand_2_out);
  nand nand_7 (nand_7_out, nand_3_out, nand_3_out);
  nand nand_8 (nand_8_out, nand_4_out, nand_4_out);
  nand nand_9 (nand_9_out, nand_5_out, nand_6_out);
  nand nand_10 (nand_10_out, nand_7_out, nand_8_out);
  nand nand_11 (nand_11_out, nand_9_out, nand_9_out);
  nand nand_12 (nand_12_out, nand_10_out, nand_10_out);
  nand nand_13 (nand_13_out, nand_11_out, nand_12_out);
  nand nand_14 (nand_14_out, nand_13_out, nand_13_out);
  nand nand_15 (nand_15_out, nand_14_out, in_9);
  nand nand_16 (out_10, nand_15_out, nand_15_out);
endmodule

module seldel (
  input  D1,
  input  D2,
  input  C1,
  input  C2,
  output D,
  output C
);

  wire nand_1_out, nand_2_out, nand_3_out, nand_4_out, nand_5_out, nand_6_out, nand_8_out;

  nand nand_1 (nand_1_out, C2, C2);
  nand nand_2 (nand_2_out, nand_1_out, D1);
  nand nand_3 (nand_3_out, C2, D2);
  nand nand_4 (nand_4_out, C1, C1);
  nand nand_5 (nand_5_out, C2, C2);
  nand nand_6 (nand_6_out, nand_2_out, nand_3_out);
  nand nand_7 (C, nand_4_out, nand_5_out);
  nand nand_8 (nand_8_out, nand_6_out, nand_6_out);
  nand nand_9 (D, nand_8_out, nand_8_out);

  // Notes on the sheet:
  //   Select-Delay
endmodule
